// Logisim project control_logic.circ as structural Verilog: 1 circuit, main circuit control_logic
module control_logic (
  input  [31:0] inst,
  input  BrEq,
  input  BrLt,
  output PCSel,
  output RegWEn,
  output [2:0] ImmSel,
  output BrUn,
  output ASel,
  output BSel,
  output [3:0] ALUSel,
  output MemRW,
  output [1:0] WBSel,
  output CSRSel,
  output CSRWen
);

  wire add, add_mul_sub, addi, andd, mul, mulh, mulhu, not_1_out, not_2_out, not_3_out, not_4_out, not_5_out,
       not_6_out, not_7_out, not_8_out, not_9_out, not_10_out, not_11_out, not_12_out, or_2_out, ori, orr,
       R_Type, sll_mulh, slli, slll, slt, slti, sraa, srai, srl_sra, srli, srli_srai, srll, sub, xori, xorr;

  Demultiplexer #(.enable("false"), .select(5)) demultiplexer_1 (
    .out4(BSel), .out12(R_Type), .in(1'b1), .sel(5'b01100));  // open: out0, out1, out2, out3, out5, out6, out7, out8, out9, out10, out11, out13, out14, out15, out16, out17, out18, out19, out20, out21, out22, out23, out24, out25, out26, out27, out28, out29, out30, out31
  Demultiplexer #(.enable("false"), .select(3)) demultiplexer_2 (
    .out0(add_mul_sub), .out1(sll_mulh), .out2(slt), .out3(mulhu), .out4(xorr), .out5(srl_sra), .out6(orr),
    .out7(andd), .in(R_Type), .sel(3'b000));
  Demultiplexer #(.enable("false"), .select(3)) demultiplexer_3 (
    .out0(addi), .out1(slli), .out2(slti), .out4(xori), .out5(srli_srai), .out6(ori), .in(BSel), .sel(3'b000));  // open: out3, out7
  or or_1 (RegWEn, R_Type, BSel);
  or or_2 (or_2_out, R_Type, BSel);
  assign WBSel = {{1{1'b0}}, or_2_out};  // Bit_Extender bit_extender_1
  Demultiplexer #(.enable("false"), .select(2)) demultiplexer_4 (
    .out0(add), .out1(mul), .out2(sub), .in(add_mul_sub), .sel(2'b10));  // open: out3
  not not_1 (not_1_out, mul);
  not not_2 (not_2_out, sub);
  and and_1 (ALUSel[3], ~add, ~not_1_out, ~not_2_out, ~slll, ~not_3_out, ~slt, ~not_4_out, ~andd, ~orr, ~srll, ~sraa, ~xorr);  // AND_Gate
  not not_3 (not_3_out, mulh);
  not not_4 (not_4_out, mulhu);
  not not_5 (not_5_out, sub);
  not not_6 (not_6_out, slll);
  and and_2 (ALUSel[2], ~add, ~mul, ~not_5_out, ~not_6_out, ~mulh, ~not_7_out, ~mulhu, ~andd, ~orr, ~not_8_out, ~not_9_out, ~xorr);  // AND_Gate
  not not_7 (not_7_out, slt);
  not not_8 (not_8_out, srll);
  not not_9 (not_9_out, sraa);
  and and_3 (ALUSel[2], ~addi, slli, slti, ~xori, srli, srai, ~ori);  // AND_Gate
  Demultiplexer #(.enable("false")) demultiplexer_5 (.out0(slll), .out1(mulh), .in(sll_mulh), .sel(1'b0));
  and and_4 (ALUSel[1], ~add, ~mul, ~sub, ~slll, ~mulh, ~slt, ~mulhu, ~andd, ~not_10_out, ~srll, ~sraa, ~not_11_out);  // AND_Gate
  not not_10 (not_10_out, orr);
  and and_5 (ALUSel[1], ~addi, slli, slti, xori, ~srli, ~srai, ori);  // AND_Gate
  not not_11 (not_11_out, xorr);
  and and_6 (ALUSel[0], ~add, ~mul, ~sub, ~slll, ~mulh, ~slt, ~mulhu, ~not_12_out, ~orr, ~srll, ~sraa, ~xorr);  // AND_Gate
  not not_12 (not_12_out, andd);
  and and_7 (ALUSel[0], ~addi, ~slli, slti, xori, ~srli, srai, ~ori);  // AND_Gate
  Demultiplexer #(.enable("false")) demultiplexer_6 (.out0(srll), .out1(sraa), .in(srl_sra), .sel(1'b1));
  Demultiplexer #(.enable("false")) demultiplexer_7 (.out0(srli), .out1(srai), .in(srli_srai), .sel(1'b1));

  assign ASel = 1'b0;
  assign ImmSel = 3'b000;
  assign MemRW = 1'b0;
  assign PCSel = 1'b0;

  // Other names for the same wires on the sheet: I_Type_Normal = BSel

  // Notes on the sheet:
  //   INPUTS to your circuit
  //   R-Type
  //   DON'T CHANGE THE LOCATIONS OF THE INPUTS AND OUTPUTS!
  //   OUTPUT from your circuit
  //   add/mul/sub
  //   add/mul/sub
  //   and
  //   sll/mulh
  //   or
  //   or
  //   slt
  //   srl/sra
  //   srl/sra
  //   mulhu
  //   xor
  //   xor
endmodule
